# Fritzing sketch schematic (saved by Fritzing 0.9.3b)
breadboards: 1

parts:
  R = Resistor [tolerance=±5% resistance=200 package=THT]
  LED = LED - 3mm [color="Red (660nm)" package="3 mm [THT]"]
  Part1 = Arduino Uno (Rev3)

nets:
  N1: R.Pin_0, Part1.D10_PWM/SS
  N2: R.Pin_1, LED.anode
  GND: LED.cathode, Part1.GND
